// Logisim project control_logic.circ as structural Verilog: 1 circuit, main circuit control_logic
module control_logic (
  input  [31:0] inst,
  input  BrEq,
  input  BrLt,
  output PCSel,
  output RegWEn,
  output [2:0] ImmSel,
  output BrUn,
  output ASel,
  output BSel,
  output [3:0] ALUSel,
  output MemRW,
  output [1:0] WBSel,
  output CSRSel,
  output CSRWen
);

  wire demultiplexer_1_out0, demultiplexer_1_out4, demultiplexer_1_out5, demultiplexer_1_out13,
       demultiplexer_1_out25, demultiplexer_1_out28, I, I1, I2, R, S, SB, U, UJ;
  wire [0:0] WBSelI;
  wire [3:0] ALUSelI, ALUSelR, multiplexer_6_out, multiplexer_7_out, multiplexer_8_out, multiplexer_10_out,
       multiplexer_11_out;

  Demultiplexer #(.select(5)) demultiplexer_1 (
    .out0(demultiplexer_1_out0), .out4(demultiplexer_1_out4), .out5(demultiplexer_1_out5), .out8(S),
    .out12(R), .out13(demultiplexer_1_out13), .out24(SB), .out25(demultiplexer_1_out25), .out27(UJ),
    .out28(demultiplexer_1_out28), .in(1'b1), .sel(inst[6:2]));  // open: out1, out2, out3, out6, out7, out9, out10, out11, out14, out15, out16, out17, out18, out19, out20, out21, out22, out23, out26, out29, out30, out31
  or or_1 (I1, demultiplexer_1_out0, demultiplexer_1_out4);
  or or_2 (I2, demultiplexer_1_out25, demultiplexer_1_out28);
  Multiplexer multiplexer_1 (.in0(1'b0), .in1(1'b0), .out(ASel), .sel(I));
  or or_3 (U, demultiplexer_1_out5, demultiplexer_1_out13);
  or or_4 (I, I1, I2);
  Multiplexer multiplexer_2 (.in0(1'b0), .in1(1'b1), .out(BSel), .sel(I));
  Multiplexer #(.width(4)) multiplexer_3 (.in0(ALUSelR), .in1(ALUSelI), .out(ALUSel), .sel(I));
  Multiplexer multiplexer_4 (.in0(1'b0), .in1(1'b0), .out(MemRW), .sel(I));
  Multiplexer #(.width(2)) multiplexer_5 (.in0(2'b00), .in1({1'b0, WBSelI[0]}), .out(WBSel), .sel(I));
  Multiplexer #(.select(2), .width(4)) multiplexer_6 (
    .in0(4'b0000), .in1(4'b1100), .in2(4'b1010), .out(multiplexer_6_out), .sel({inst[25], inst[30]}));  // open: in3
  Multiplexer #(.width(4)) multiplexer_7 (.in0(4'b0110), .in1(4'b1110), .out(multiplexer_7_out), .sel(inst[25]));
  Multiplexer #(.width(4)) multiplexer_8 (.in0(4'b0100), .in1(4'b0101), .out(multiplexer_8_out), .sel(inst[30]));
  Multiplexer #(.select(3), .width(4)) multiplexer_9 (
    .in0(multiplexer_6_out), .in1(multiplexer_7_out), .in2(4'b0111), .in3(4'b1011), .in4(4'b0011),
    .in5(multiplexer_8_out), .in6(4'b0010), .in7(4'b0001), .out(ALUSelR), .sel(inst[14:12]));
  not not_1 (WBSelI[0], inst[4]);
  Multiplexer #(.width(4)) multiplexer_10 (.in0(4'b0100), .in1(4'b0101), .out(multiplexer_10_out), .sel(inst[30]));
  Multiplexer #(.select(3), .width(4)) multiplexer_11 (
    .in0(4'b0000), .in1(4'b0110), .in2(4'b0111), .in4(4'b0011), .in5(multiplexer_10_out), .in6(4'b0010),
    .in7(4'b0001), .out(multiplexer_11_out), .sel(inst[14:12]));  // open: in3
  Multiplexer #(.width(4)) multiplexer_12 (.in0(4'b0000), .in1(multiplexer_11_out), .out(ALUSelI), .sel(inst[4]));

  assign ImmSel = 3'b000;
  assign PCSel = 1'b0;
  assign RegWEn = 1'b1;

  // Other names for the same wires on the sheet: funct7[6:0] = inst[31:25]; opcode0[4:0] = inst[6:2];
  //   funct3[2:0] = inst[14:12]

  // Notes on the sheet:
  //   INPUTS to your circuit
  //   Get instruction-type
  //   OUTPUT from your circuit
  //   R-type operations
  //   I-type operations
endmodule
