// Logisim project cpu.circ as structural Verilog: 1 circuit, main circuit cpu
module cpu (
  input  clk,
  input  [31:0] INSTRUCTION,
  input  [31:0] READ_DATA,
  output [31:0] WRITE_ADDRESS,
  output [31:0] PROGRAM_COUNTER,
  output [31:0] ra,
  output [31:0] sp,
  output [31:0] t0,
  output [31:0] t1,
  output [31:0] t2,
  output [31:0] s0,
  output [31:0] s1,
  output [31:0] a0,
  output [31:0] tohost,
  output [3:0] WRITE_ENABLE,
  output [31:0] WRITE_DATA
);

  wire MemRW;
  wire [1:0] WBSel;
  wire [2:0] funct3;
  wire [3:0] ALUSel;
  wire [31:0] adder_1_out, alu_res, imm0, inst, pc, reg1, reg2, wb;

  Adder #(.width(32)) adder_1 (.a(PROGRAM_COUNTER), .b(32'h4), .out(adder_1_out));  // open: cin, cout
  Register #(.width(32)) u_PC (.D(adder_1_out), .en(1'b1), .clk(clk), .Q(PROGRAM_COUNTER));  // open: clr
  control_logic control_logic_1 (
    .ALUSel(ALUSel), .MemRW(MemRW), .WBSel(WBSel));  // open: inst, BrEq, BrLt, CSRWen, PCSel, RegWEn, ImmSel, BrUn, ASel, BSel, CSRSel
  Register #(.width(32)) register_1 (.D(PROGRAM_COUNTER), .en(1'b1), .clk(clk), .Q(pc));  // open: clr
  Register #(.width(32)) register_2 (
    .D(INSTRUCTION), .en(1'b1), .clk(clk), .Q({inst[31:15], funct3, inst[11:0]}));  // open: clr
  regfile regfile_1 (
    .rs1(inst[19:15]), .rs2(inst[24:20]), .rd(inst[11:7]), .Write_Data(wb), .RegWEn(MemRW), .clk(clk),
    .ra(ra), .sp(sp), .t0(t0), .t1(t1), .t2(t2), .s0(s0), .s1(s1), .a0(a0), .Read_Data_1(reg1),
    .Read_Data_2(reg2));
  imm_gen imm_gen_1 (.inst({inst[31:15], funct3, inst[11:0]}), .ImmSel(3'b000), .imm(imm0));
  alu alu_1 (.A(reg1), .B(reg2), .ALUSel(ALUSel), .Result(alu_res));
  // branch_comp branch_comp_1: pin names not known
  Multiplexer #(.select(2), .width(32)) multiplexer_1 (
    .in0(alu_res), .in1(READ_DATA), .out(wb), .sel(WBSel));  // open: in2, in3
  csr csr_1 (.tohost(tohost));  // open: CSR_address, CSR_din, CSR_WE, clk

  // Other names for the same wires on the sheet: opcode[6:0] = inst[6:0]; rd[4:0] = inst[11:7]; inst[14:12] = funct3;
  //   rs1[4:0] = inst[19:15]; rs2[4:0] = inst[24:20]

  // Notes on the sheet:
  //   Output to IMEM
  //   IMEM (do **NOT** move this)
  //   Inputs from IMEM
  //   Inputs/Outputs for testing. Do **NOT** move these.
  //   Outputs To DMEM
  //   DMEM (do **NOT** move this)
  //   Inputs From DMEM
endmodule
